# Fritzing sketch led (saved by Fritzing 0.9.6b)
breadboards: 1

parts:
  IC3 = DIP - 28 pins [chip_label=IC package="DIP (Dual Inline) [THT]"]
  LED1 = smd LED [color="Red (633nm)" package="0805 [SMD]"]
  R1 = Resistor [tolerance=±5% resistance=330 package="0805 [SMD]"]

nets:
  N1: IC3.GND, R1.Pin_0
  N2: LED1.cathode, R1.Pin_1

custom parts:
  DIP - 28 pins: A DIP stand-in part for whatever IC you want. With 28 pins on a 300mil dual inline package (DIP) footprint.
